# Fritzing sketch IR-Fernbedienung (saved by Fritzing 0.9.3b)
circuit board: 7.31799cm x 3.06543cm
breadboards: 1

parts:
  ESP01 = ESP8266 WiFi Module [part_number=ESP8266]
  Relais = KY-019 5V Relay Module [package="Breakout board"]
  1kΩ = Resistor [tolerance=±5% resistance=1k package=THT]
  1kΩ_2 = Resistor [tolerance=±5% resistance=1k package=THT]
  BC337 = NPN-Transistor [package="TO92 [THT]"]
  IR_LED = LED - 3mm [color="Infrared (940nm)" package="3 mm [THT]"]
  5V_Power = Power plug
  ASM11117_3_3V = Step Down 5V to 3.3V [package="DIP (Dual Inline) [THT]"]
  BC307B = PNP-Transistor [package="TO92 [THT]"]

nets:
  N1: ESP01.RXD, 1kΩ_2.Pin_0
  N2: ESP01.VCC, ASM11117_3_3V.OUT
  N3: ESP01.GPIO_2, 1kΩ.Pin_1
  GND: ESP01.GND, BC337.E, 5V_Power.GND, ASM11117_3_3V.GND, BC307B.E
  N4: Relais.S, Relais.+, IR_LED.anode, 5V_Power.VCC, ASM11117_3_3V.IN
  N5: Relais.-, BC307B.C
  N6: 1kΩ.Pin_0, BC307B.B
  N7: 1kΩ_2.Pin_1, BC337.B
  N8: BC337.C, IR_LED.cathode

notes:
  5V
  3.3V
  USB aus dem PC ist evtl. zu schwach.
  USB-Netzteil verwenden. Z.B. Handy-Lade-Adapter.
  D0 und D1 des ESP01 können nicht sinnvoll genutzt werden. D0 muss beim booten auf high gelegt werden. Das ist nicht ohne weiteres möglich, wenn D0 dann im weiteren mit einer Funktion genutzt werden soll.

custom parts:
  ESP8266 WiFi Module: Generic WiFi Module based on the ESP8266 with onboard PCB antenna and UART communications
  KY-019 5V Relay Module: KY-019 5V Relay module, used to control AC circuits. (Special thanks to vanepp for fixing the PCB holes and other errors)
  Step Down 5V to 3.3V: Step Down 5V to 3.3V 1A

// code stored in the sketch: Relais_schalten.ino

